# Fritzing sketch circuito-montagem-projeto-jogo-da-memoria-com-arduino (saved by Fritzing 0.9.3b)
breadboards: 1

parts:
  Componente1 = Arduino Uno (Rev3) - ICSP
  Componente2 = LCD1602-I2C
  J1 = Piezo Speaker
  S1 = Pushbutton [package="[THT]"]
  S2 = Pushbutton [package="[THT]"]
  S3 = Pushbutton [package="[THT]"]
  S4 = Pushbutton [package="[THT]"]
  S5 = Pushbutton [package="[THT]"]
  LED1 = LED - 3mm [color="Blue (430nm)" package="3 mm [THT]"]
  LED2 = LED - 3mm [color="Red (633nm)" package="3 mm [THT]"]
  LED3 = LED - 3mm [color="Yellow (595nm)" package="3 mm [THT]"]
  LED4 = LED - 3mm [color="Green (570nm)" package="3 mm [THT]"]
  U1 = POT [package=pot_alpha_rv16af-20]
  BAT1 = BC9VPC [package=bc9vpc]
  JACK1 = 2.1mm Barrel Jack with Terminal Block
  R1 = Resistor [tolerance=±5% resistance=220 package="0805 [SMD]"]
  R2 = Resistor [tolerance=±5% resistance=220 package="0805 [SMD]"]
  R3 = Resistor [tolerance=±5% resistance=220 package="0805 [SMD]"]
  R4 = Resistor [tolerance=±5% resistance=220 package="0805 [SMD]"]

nets:
  N1: Componente1.A0, U1.S
  N2: Componente1.A4/SDA, Componente2.SDA
  N3: Componente1.A5/SCL, Componente2.SCL
  N4: Componente1.D8, R2.Pin_1
  N5: Componente1.D9_PWM, S2.Pin_1, S2.Pin_2
  N6: Componente1.D10_PWM/SS, R3.Pin_1
  N7: Componente1.D11_PWM/MOSI, S1.Pin_1, S1.Pin_2
  N8: Componente1.D12/MISO, S4.Pin_1, S4.Pin_2
  N9: Componente1.D3_PWM, J1.pin2
  N10: Componente1.D4, R1.Pin_1
  N11: Componente1.D5_PWM, S5.Pin_1, S5.Pin_2
  N12: Componente1.D6_PWM, R4.Pin_1
  N13: Componente1.D7, S3.Pin_1, S3.Pin_2
  5V: Componente1.5V, Componente2.VCC
  GND: Componente1.GND, Componente2.GND, J1.pin1, S1.Pin_3, S1.Pin_4, S2.Pin_3, S2.Pin_4, S3.Pin_3, S3.Pin_4, S4.Pin_3, S4.Pin_4, S5.Pin_3, S5.Pin_4, LED1.cathode, LED2.cathode, LED3.cathode, LED4.cathode, U1.A, U1.E
  N14: LED1.anode, R1.Pin_0
  N15: LED2.anode, R3.Pin_0
  N16: LED3.anode, R2.Pin_0
  N17: LED4.anode, R4.Pin_0
  N18: BAT1.V+, JACK1.POS
  N19: BAT1.V-, JACK1.NEG

custom parts:
  LCD1602-I2C: A standard character display, usually with 2x16 characters. Comes in many colors with LCM1602 IIC attached.
